# Fritzing sketch Circuito (saved by Fritzing 0.9.3b)
breadboards: 1

parts:
  Componente1 = Arduino Uno (Rev3) - ICSP
  Componente2 = Arduino Uno (Rev3) - ICSP
  BAT1 = Battery Holders [package=battery-aa-panel]  # not connected
  R1 = Resistor [tolerance=±5% resistance=220 package=THT]
  JP1 = FTDI_BASIC [package=ftdi_basic]  # not connected

nets:
  N1: Componente1.D0/RX, Componente2.D0/RX
  N2: Componente1.D1/TX, Componente2.D1/TX
  N3: Componente1.D2, Componente2.5V, R1.Pin_1
  GND: Componente1.GND, Componente2.GND, R1.Pin_0
